# Fritzing sketch Pico 18B20 (saved by Fritzing 1.0.1rc)
breadboards: 1

parts:
  Pico_H1 = Raspberry Pi Pico H
  DS1 = DS18B20 Temperature Sensor [part_number=DS18B20]

nets:
  N1: Pico_H1.VSYS, Pico_H1.GP21, Pico_H1.GP7, DS1.R/VCC
  N2: Pico_H1.ADC_VREF, Pico_H1.GP18
  N3: Pico_H1.AGND, Pico_H1.GP11, DS1.G/GND
  N4: Pico_H1.GND, Pico_H1.GP2
  N5: Pico_H1.GP9, DS1.Y/DQ

custom parts:
  Raspberry Pi Pico H: Raspberry Pi Pico H. Based around the RP2040 microcontroller the Pico H is a low cost microcontroller device bringing Raspberry Pi quality, cost, and easy of use to the microcontroller space.
  DS18B20 Temperature Sensor: The DS18B20 digital thermometer provides 9-bit to 12-bit Celsius temperature measurements and has an alarm function with nonvolatile user-programmable upper and lower trigger points. The DS18B20 communicates over a 1-Wire bus that by definition requires only one data line (and ground) for communication with a central microprocessor. In addition, the DS18B20 can derive power directly from the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
