# Fritzing sketch Pico push button (saved by Fritzing 1.0.1rc)
breadboards: 1

parts:
  S1 = Push button breakout
  Pico_H1 = Raspberry Pi Pico H
  J1 = Basic Servo

nets:
  VCC: S1.S, S1.VCC, Pico_H1.VSYS, Pico_H1.GP0, J1.vcc
  GND: S1.Gnd, Pico_H1.GND, J1.gnd
  N1: Pico_H1.GP1, J1.pulse

custom parts:
  Push button breakout: Elgoo sensor kit breakout with a push to make button
  Raspberry Pi Pico H: Raspberry Pi Pico H. Based around the RP2040 microcontroller the Pico H is a low cost microcontroller device bringing Raspberry Pi quality, cost, and easy of use to the microcontroller space.
